# Fritzing sketch Diagram (saved by Fritzing 0.9.6b)

parts:
  Part1 = Arduino Uno (Rev3) - ICSP
  INA1 = INA219_DC_Current_Sensor_Breakout
  R1 = Resistor [tolerance=±5% resistance=33 power=1.5 package="0402 [SMD]"]
  Part2 = Solar_Cell
  L298N1 = L298N motor driver
  INA2 = INA219_DC_Current_Sensor_Breakout
  R2 = Resistor [tolerance=±5% resistance=33 power=1.5 package="0402 [SMD]"]
  Part3 = Solar_Cell
  S1 = Toggle Switch [package=THT]
  S2 = Toggle Switch [package=THT]
  M1 = DC Motor
  M2 = DC Motor
  T1 = LM35 Temperature Sensor [package="TO92 [THT]"]
  R3 = Photocell (LDR) [package=THT]
  R4 = Resistor [tolerance=±5% resistance=1000 package="0402 [SMD]"]

nets:
  N1: Part1.A0, R4.Pin_1
  N2: Part1.A1, T1.Vout
  N3: Part1.A4/SDA, INA1.connector4, INA2.connector4
  N4: Part1.A5/SCL, INA1.connector3, INA2.connector3
  N5: Part1.ICSP_MOSI, Part1.D11_PWM/MOSI, L298N1.connector11
  N6: Part1.D8, L298N1.connector15
  N7: Part1.D9_PWM, L298N1.connector14
  N8: Part1.D10_PWM/SS, L298N1.connector13
  GND: Part1.GND, INA1.connector2, INA2.connector2, S1.L1, S2.L1, T1.GND
  N9: Part1.D2, S1.COM
  N10: Part1.D3_PWM, S2.COM
  N11: Part1.D6_PWM, L298N1.connector12
  N12: Part1.D7, L298N1.connector16
  N13: Part1.5V, INA1.connector1, INA2.connector1, T1.+Vs, R3.pin_0
  N14: INA1.connector7, Part2.connector1
  N15: INA1.connector8, R1.Pin_1
  N16: R1.Pin_0, Part2.connector0
  N17: L298N1.connector0, M2.pin_2
  N18: L298N1.connector1, M2.pin_1
  N19: L298N1.connector2, M1.pin_2
  N20: L298N1.connector4, M1.pin_1
  N21: INA2.connector7, Part3.connector1
  N22: INA2.connector8, R2.Pin_1
  N23: R2.Pin_0, Part3.connector0
  N24: R3.pin_1, R4.Pin_0

notes:
  Fonte DC 5V
